// Logisim project sagui_em_bando.circ as structural Verilog: 12 circuits, main circuit main
module main (
);

  wire adder_1_cout, and_1_out, c_register_bank_seq_1_blk, c_register_bank_simd_1_blk, clock_1_out,
       idecoder_1_branch, idecoder_1_imm, idecoder_1_load, idecoder_1_rwe, idecoder_1_simd, idecoder_1_store,
       multiplexer_2_out, multiplexer_3_out, multiplexer_7_out, multiplexer_8_out, multiplexer_9_out,
       multiplexer_10_out, multiplexer_11_out, multiplexer_12_out, multiplexer_13_out, not_1_out, or_1_out,
       or_2_out, or_3_out, or_4_out, pipe_exmd_seq_1_branch_out, pipe_exmd_seq_1_load_out,
       pipe_exmd_seq_1_rwe_out, pipe_exmd_seq_1_store_out, pipe_exmd_simd_1_load_out,
       pipe_exmd_simd_1_rwe_out, pipe_exmd_simd_1_store_out, pipe_mdwb_seq_1_load_out,
       pipe_mdwb_seq_1_rwe_out, pipe_mdwb_simd_1_load_out, pipe_mdwb_simd_1_rwe_out,
       pipe_reex_seq_1_branch_out, pipe_reex_seq_1_load_out, pipe_reex_seq_1_rwe_out,
       pipe_reex_seq_1_store_out, pipe_reex_simd_1_load_out, pipe_reex_simd_1_rwe_out,
       pipe_reex_simd_1_store_out, Reset_out;
  wire [1:0] multiplexer_5_out, multiplexer_6_out, multiplexer_14_out, multiplexer_15_out,
       multiplexer_17_out, multiplexer_18_out, multiplexer_19_out, multiplexer_20_out,
       pipe_exmd_seq_1_rd_out, pipe_exmd_simd_1_rd_out, pipe_mdwb_seq_1_rd_out, pipe_mdwb_simd_1_rd_out,
       pipe_reex_seq_1_rd_out, pipe_reex_simd_1_rd_out;
  wire [2:0] MI_data_2, pipe_reex_seq_1_opcode_out, pipe_reex_simd_1_opcode_out;
  wire [7:0] adder_1_out, alu_seq_1_r, alu_simd_1_r, alu_simd_2_r, alu_simd_3_r, alu_simd_4_r,
       bit_extender_1_out, c_register_bank_seq_1_da, c_register_bank_seq_1_db, c_register_bank_simd_1_da0,
       c_register_bank_simd_1_da1, c_register_bank_simd_1_da2, c_register_bank_simd_1_da3,
       c_register_bank_simd_1_db0, c_register_bank_simd_1_db1, c_register_bank_simd_1_db2,
       c_register_bank_simd_1_db3, MD_dout, MI_data, multiplexer_1_out, multiplexer_4_out,
       multiplexer_16_out, multiplexer_21_out, multiplexer_22_out, multiplexer_23_out, multiplexer_24_out,
       multiplexer_25_out, multiplexer_26_out, multiplexer_27_out, multiplexer_28_out, multiplexer_29_out,
       multiplexer_30_out, PC_q, pipe_exmd_seq_1_da_out, pipe_exmd_seq_1_db_out, pipe_exmd_simd_1_da0_out,
       pipe_exmd_simd_1_da1_out, pipe_exmd_simd_1_da2_out, pipe_exmd_simd_1_da3_out,
       pipe_exmd_simd_1_db0_out, pipe_exmd_simd_1_db1_out, pipe_exmd_simd_1_db2_out,
       pipe_exmd_simd_1_db3_out, pipe_mdwb_seq_1_md_out, pipe_mdwb_seq_1_rv_out, pipe_mdwb_simd_1_m0_out,
       pipe_mdwb_simd_1_m1_out, pipe_mdwb_simd_1_m2_out, pipe_mdwb_simd_1_m3_out, pipe_mdwb_simd_1_r0_out,
       pipe_mdwb_simd_1_r1_out, pipe_mdwb_simd_1_r2_out, pipe_mdwb_simd_1_r3_out, pipe_reex_seq_1_da_out,
       pipe_reex_seq_1_db_out, pipe_reex_simd_1_da0_out, pipe_reex_simd_1_da1_out, pipe_reex_simd_1_da2_out,
       pipe_reex_simd_1_da3_out, pipe_reex_simd_1_db0_out, pipe_reex_simd_1_db1_out,
       pipe_reex_simd_1_db2_out, pipe_reex_simd_1_db3_out, ram_1_dout, ram_2_dout, ram_3_dout, ram_4_dout;

  Adder adder_1 (.a(PC_q), .b(8'h1), .out(adder_1_out), .cin(1'b0), .cout(adder_1_cout));
  LED led_1 (.in(adder_1_cout));
  Register PC (.D(multiplexer_1_out), .en(not_1_out), .clk(clock_1_out), .Q(PC_q), .clr(Reset_out));
  Multiplexer #(.width(8)) multiplexer_1 (
    .in0(adder_1_out), .in1(pipe_exmd_seq_1_db_out), .out(multiplexer_1_out), .sel(pipe_exmd_seq_1_branch_out));
  not not_1 (not_1_out, or_1_out);
  ROM MI (.addr(PC_q), .data({MI_data[7], MI_data_2, MI_data[3:0]}));
  Button Reset (.out(Reset_out));
  Clock clock_1 (.out(clock_1_out));
  // Probe on {MI_data[7], MI_data_2}
  assign bit_extender_1_out = {{4{MI_data[3]}}, MI_data[3:0]};  // Bit_Extender bit_extender_1
  idecoder idecoder_1 (
    .opcode({MI_data[7], MI_data_2}), .load(idecoder_1_load), .rwe(idecoder_1_rwe),
    .branch(idecoder_1_branch), .simd(idecoder_1_simd), .imm(idecoder_1_imm), .store(idecoder_1_store));
  Multiplexer multiplexer_2 (.in0(idecoder_1_branch), .in1(1'b0), .out(multiplexer_2_out), .sel(idecoder_1_simd));
  Multiplexer multiplexer_3 (.in0(idecoder_1_imm), .in1(1'b0), .out(multiplexer_3_out), .sel(idecoder_1_simd));
  Multiplexer #(.width(8)) multiplexer_4 (
    .in0(bit_extender_1_out), .in1({8{1'b0}}), .out(multiplexer_4_out), .sel(idecoder_1_simd));
  Multiplexer #(.width(2)) multiplexer_5 (
    .in0(MI_data[3:2]), .in1(2'b00), .out(multiplexer_5_out), .sel(idecoder_1_simd));
  Multiplexer #(.width(2)) multiplexer_6 (
    .in0(MI_data[1:0]), .in1(2'b00), .out(multiplexer_6_out), .sel(idecoder_1_simd));
  Multiplexer multiplexer_7 (.in0(idecoder_1_store), .in1(1'b0), .out(multiplexer_7_out), .sel(idecoder_1_simd));
  Multiplexer multiplexer_8 (.in0(idecoder_1_rwe), .in1(1'b0), .out(multiplexer_8_out), .sel(idecoder_1_simd));
  Multiplexer multiplexer_9 (.in0(idecoder_1_load), .in1(1'b0), .out(multiplexer_9_out), .sel(idecoder_1_simd));
  Multiplexer multiplexer_10 (.in0(1'b0), .in1(idecoder_1_imm), .out(multiplexer_10_out), .sel(idecoder_1_simd));
  Multiplexer multiplexer_11 (.in0(1'b0), .in1(idecoder_1_rwe), .out(multiplexer_11_out), .sel(idecoder_1_simd));
  Multiplexer multiplexer_12 (.in0(1'b0), .in1(idecoder_1_store), .out(multiplexer_12_out), .sel(idecoder_1_simd));
  Multiplexer multiplexer_13 (.in0(1'b0), .in1(idecoder_1_load), .out(multiplexer_13_out), .sel(idecoder_1_simd));
  Multiplexer #(.width(2)) multiplexer_14 (
    .in0(2'b00), .in1(MI_data[3:2]), .out(multiplexer_14_out), .sel(idecoder_1_simd));
  Multiplexer #(.width(2)) multiplexer_15 (
    .in0(2'b00), .in1(MI_data[1:0]), .out(multiplexer_15_out), .sel(idecoder_1_simd));
  Multiplexer #(.width(8)) multiplexer_16 (
    .in0({8{1'b0}}), .in1(bit_extender_1_out), .out(multiplexer_16_out), .sel(idecoder_1_simd));
  Multiplexer #(.width(2)) multiplexer_17 (
    .in0(multiplexer_14_out), .in1(2'b01), .out(multiplexer_17_out), .sel(multiplexer_10_out));
  Multiplexer #(.width(2)) multiplexer_18 (
    .in0(multiplexer_15_out), .in1(2'b01), .out(multiplexer_18_out), .sel(multiplexer_10_out));
  Multiplexer #(.width(2)) multiplexer_19 (
    .in0(multiplexer_5_out), .in1(2'b01), .out(multiplexer_19_out), .sel(multiplexer_3_out));
  Multiplexer #(.width(2)) multiplexer_20 (
    .in0(multiplexer_6_out), .in1(2'b01), .out(multiplexer_20_out), .sel(multiplexer_3_out));
  c_register_bank_seq c_register_bank_seq_1 (
    .R(Reset_out), .RC(pipe_exmd_seq_1_branch_out), .RA(multiplexer_19_out), .RB(multiplexer_20_out),
    .FWE(multiplexer_8_out), .FRD(multiplexer_19_out), .WE(pipe_mdwb_seq_1_rwe_out),
    .RD(pipe_mdwb_seq_1_rd_out), .D(multiplexer_26_out), .Clk(clock_1_out), .Blk(c_register_bank_seq_1_blk),
    .DA(c_register_bank_seq_1_da), .DB(c_register_bank_seq_1_db));
  or or_1 (or_1_out, c_register_bank_seq_1_blk, c_register_bank_simd_1_blk);
  c_register_bank_simd c_register_bank_simd_1 (
    .R(Reset_out), .RC(pipe_exmd_seq_1_branch_out), .RA(multiplexer_17_out), .RB(multiplexer_18_out),
    .FWE(multiplexer_11_out), .FRD(multiplexer_17_out), .WE(pipe_mdwb_simd_1_rwe_out),
    .RD(pipe_mdwb_simd_1_rd_out), .Clk(clock_1_out), .D0(multiplexer_27_out), .D1(multiplexer_28_out),
    .D2(multiplexer_29_out), .D3(multiplexer_30_out), .Blk(c_register_bank_simd_1_blk),
    .DA0(c_register_bank_simd_1_da0), .DA1(c_register_bank_simd_1_da1), .DA2(c_register_bank_simd_1_da2),
    .DA3(c_register_bank_simd_1_da3), .DB0(c_register_bank_simd_1_db0), .DB1(c_register_bank_simd_1_db1),
    .DB2(c_register_bank_simd_1_db2), .DB3(c_register_bank_simd_1_db3));
  or or_2 (or_2_out, c_register_bank_seq_1_blk, or_4_out);
  Multiplexer #(.width(8)) multiplexer_21 (
    .in0(c_register_bank_seq_1_db), .in1(multiplexer_4_out), .out(multiplexer_21_out), .sel(multiplexer_3_out));
  or or_3 (or_3_out, c_register_bank_simd_1_blk, or_4_out);
  Multiplexer #(.width(8)) multiplexer_22 (
    .in0(c_register_bank_simd_1_db0), .in1(multiplexer_16_out), .out(multiplexer_22_out),
    .sel(multiplexer_10_out));
  Multiplexer #(.width(8)) multiplexer_23 (
    .in0(c_register_bank_simd_1_db1), .in1(multiplexer_16_out), .out(multiplexer_23_out),
    .sel(multiplexer_10_out));
  Multiplexer #(.width(8)) multiplexer_24 (
    .in0(c_register_bank_simd_1_db2), .in1(multiplexer_16_out), .out(multiplexer_24_out),
    .sel(multiplexer_10_out));
  Multiplexer #(.width(8)) multiplexer_25 (
    .in0(c_register_bank_simd_1_db3), .in1(multiplexer_16_out), .out(multiplexer_25_out),
    .sel(multiplexer_10_out));
  // Probe on pipe_reex_seq_1_opcode_out
  PIPE_REEX_seq pipe_reex_seq_1 (
    .R(or_2_out), .branch_in(multiplexer_2_out), .da_in(c_register_bank_seq_1_da),
    .db_in(multiplexer_21_out), .store_in(multiplexer_7_out), .opcode_in(MI_data_2),
    .load_in(multiplexer_9_out), .rd_in(multiplexer_19_out), .rwe_in(multiplexer_8_out), .clk(clock_1_out),
    .branch_out(pipe_reex_seq_1_branch_out), .da_out(pipe_reex_seq_1_da_out),
    .db_out(pipe_reex_seq_1_db_out), .store_out(pipe_reex_seq_1_store_out),
    .opcode_out(pipe_reex_seq_1_opcode_out), .load_out(pipe_reex_seq_1_load_out),
    .rd_out(pipe_reex_seq_1_rd_out), .rwe_out(pipe_reex_seq_1_rwe_out));
  // Probe on pipe_reex_simd_1_opcode_out
  PIPE_REEX_simd pipe_reex_simd_1 (
    .R(or_3_out), .da0_in(c_register_bank_simd_1_da0), .da1_in(c_register_bank_simd_1_da1),
    .da2_in(c_register_bank_simd_1_da2), .da3_in(c_register_bank_simd_1_da3), .db0_in(multiplexer_22_out),
    .db1_in(multiplexer_23_out), .db2_in(multiplexer_24_out), .db3_in(multiplexer_25_out),
    .store_in(multiplexer_12_out), .opcode_in(MI_data_2), .load_in(multiplexer_13_out),
    .rd_in(multiplexer_17_out), .rwe_in(multiplexer_11_out), .clk(clock_1_out),
    .da0_out(pipe_reex_simd_1_da0_out), .da1_out(pipe_reex_simd_1_da1_out),
    .da2_out(pipe_reex_simd_1_da2_out), .da3_out(pipe_reex_simd_1_da3_out),
    .db0_out(pipe_reex_simd_1_db0_out), .db1_out(pipe_reex_simd_1_db1_out),
    .db2_out(pipe_reex_simd_1_db2_out), .db3_out(pipe_reex_simd_1_db3_out),
    .store_out(pipe_reex_simd_1_store_out), .opcode_out(pipe_reex_simd_1_opcode_out),
    .load_out(pipe_reex_simd_1_load_out), .rd_out(pipe_reex_simd_1_rd_out), .rwe_out(pipe_reex_simd_1_rwe_out));
  alu_seq alu_seq_1 (
    .da(pipe_reex_seq_1_da_out), .db(pipe_reex_seq_1_db_out), .opcode(pipe_reex_seq_1_opcode_out),
    .R(alu_seq_1_r));
  or or_4 (or_4_out, Reset_out, pipe_exmd_seq_1_branch_out);
  and and_1 (and_1_out, pipe_reex_seq_1_branch_out, ~alu_seq_1_r[0]);  // AND_Gate
  alu_simd alu_simd_1 (
    .da(pipe_reex_simd_1_da0_out), .db(pipe_reex_simd_1_db0_out), .opcode(pipe_reex_simd_1_opcode_out),
    .R(alu_simd_1_r));
  alu_simd alu_simd_2 (
    .da(pipe_reex_simd_1_da1_out), .db(pipe_reex_simd_1_db1_out), .opcode(pipe_reex_simd_1_opcode_out),
    .R(alu_simd_2_r));
  alu_simd alu_simd_3 (
    .da(pipe_reex_simd_1_da2_out), .db(pipe_reex_simd_1_db2_out), .opcode(pipe_reex_simd_1_opcode_out),
    .R(alu_simd_3_r));
  alu_simd alu_simd_4 (
    .da(pipe_reex_simd_1_da3_out), .db(pipe_reex_simd_1_db3_out), .opcode(pipe_reex_simd_1_opcode_out),
    .R(alu_simd_4_r));
  PIPE_EXMD_seq pipe_exmd_seq_1 (
    .R(or_4_out), .branch_in(and_1_out), .da_in(alu_seq_1_r), .db_in(pipe_reex_seq_1_db_out),
    .store_in(pipe_reex_seq_1_store_out), .load_in(pipe_reex_seq_1_load_out), .rd_in(pipe_reex_seq_1_rd_out),
    .rwe_in(pipe_reex_seq_1_rwe_out), .clk(clock_1_out), .branch_out(pipe_exmd_seq_1_branch_out),
    .da_out(pipe_exmd_seq_1_da_out), .db_out(pipe_exmd_seq_1_db_out), .store_out(pipe_exmd_seq_1_store_out),
    .load_out(pipe_exmd_seq_1_load_out), .rd_out(pipe_exmd_seq_1_rd_out), .rwe_out(pipe_exmd_seq_1_rwe_out));
  RAM #(.asyncread("true")) MD (
    .addr(pipe_exmd_seq_1_db_out), .we(pipe_exmd_seq_1_store_out), .oe(pipe_exmd_seq_1_load_out),
    .clk(clock_1_out), .din(pipe_exmd_seq_1_da_out), .dout(MD_dout));
  PIPE_EXMD_simd pipe_exmd_simd_1 (
    .R(or_4_out), .da0_in(alu_simd_1_r), .da1_in(alu_simd_2_r), .da2_in(alu_simd_3_r), .da3_in(alu_simd_4_r),
    .db0_in(pipe_reex_simd_1_db0_out), .db1_in(pipe_reex_simd_1_db1_out), .db2_in(pipe_reex_simd_1_db2_out),
    .db3_in(pipe_reex_simd_1_db3_out), .store_in(pipe_reex_simd_1_store_out),
    .load_in(pipe_reex_simd_1_load_out), .rd_in(pipe_reex_simd_1_rd_out), .rwe_in(pipe_reex_simd_1_rwe_out),
    .clk(clock_1_out), .da0_out(pipe_exmd_simd_1_da0_out), .da1_out(pipe_exmd_simd_1_da1_out),
    .da2_out(pipe_exmd_simd_1_da2_out), .da3_out(pipe_exmd_simd_1_da3_out),
    .db0_out(pipe_exmd_simd_1_db0_out), .db1_out(pipe_exmd_simd_1_db1_out),
    .db2_out(pipe_exmd_simd_1_db2_out), .db3_out(pipe_exmd_simd_1_db3_out),
    .store_out(pipe_exmd_simd_1_store_out), .load_out(pipe_exmd_simd_1_load_out),
    .rd_out(pipe_exmd_simd_1_rd_out), .rwe_out(pipe_exmd_simd_1_rwe_out));
  RAM #(.asyncread("true")) ram_1 (
    .addr(pipe_exmd_simd_1_db0_out), .we(pipe_exmd_simd_1_store_out), .oe(pipe_exmd_simd_1_load_out),
    .clk(clock_1_out), .din(pipe_exmd_simd_1_da0_out), .dout(ram_1_dout));
  RAM #(.asyncread("true")) ram_2 (
    .addr(pipe_exmd_simd_1_db1_out), .we(pipe_exmd_simd_1_store_out), .oe(pipe_exmd_simd_1_load_out),
    .clk(clock_1_out), .din(pipe_exmd_simd_1_da1_out), .dout(ram_2_dout));
  RAM #(.asyncread("true")) ram_3 (
    .addr(pipe_exmd_simd_1_db2_out), .we(pipe_exmd_simd_1_store_out), .oe(pipe_exmd_simd_1_load_out),
    .clk(clock_1_out), .din(pipe_exmd_simd_1_da2_out), .dout(ram_3_dout));
  RAM #(.asyncread("true")) ram_4 (
    .addr(pipe_exmd_simd_1_db3_out), .we(pipe_exmd_simd_1_store_out), .oe(pipe_exmd_simd_1_load_out),
    .clk(clock_1_out), .din(pipe_exmd_simd_1_da3_out), .dout(ram_4_dout));
  PIPE_MDWB_seq pipe_mdwb_seq_1 (
    .R(or_4_out), .load_in(pipe_exmd_seq_1_load_out), .rv_in(pipe_exmd_seq_1_da_out), .md_in(MD_dout),
    .rd_in(pipe_exmd_seq_1_rd_out), .rwe_in(pipe_exmd_seq_1_rwe_out), .clk(clock_1_out),
    .load_out(pipe_mdwb_seq_1_load_out), .rv_out(pipe_mdwb_seq_1_rv_out), .md_out(pipe_mdwb_seq_1_md_out),
    .rd_out(pipe_mdwb_seq_1_rd_out), .rwe_out(pipe_mdwb_seq_1_rwe_out));
  Multiplexer #(.width(8)) multiplexer_26 (
    .in0(pipe_mdwb_seq_1_rv_out), .in1(pipe_mdwb_seq_1_md_out), .out(multiplexer_26_out),
    .sel(pipe_mdwb_seq_1_load_out));
  PIPE_MDWB_simd pipe_mdwb_simd_1 (
    .R(or_4_out), .m0_in(ram_1_dout), .r0_in(pipe_exmd_simd_1_da0_out), .m1_in(ram_2_dout),
    .r1_in(pipe_exmd_simd_1_da1_out), .m2_in(ram_3_dout), .r2_in(pipe_exmd_simd_1_da2_out),
    .m3_in(ram_4_dout), .r3_in(pipe_exmd_simd_1_da3_out), .load_in(pipe_exmd_simd_1_load_out),
    .rd_in(pipe_exmd_simd_1_rd_out), .rwe_in(pipe_exmd_simd_1_rwe_out), .clk(clock_1_out),
    .m0_out(pipe_mdwb_simd_1_m0_out), .r0_out(pipe_mdwb_simd_1_r0_out), .m1_out(pipe_mdwb_simd_1_m1_out),
    .r1_out(pipe_mdwb_simd_1_r1_out), .m2_out(pipe_mdwb_simd_1_m2_out), .r2_out(pipe_mdwb_simd_1_r2_out),
    .m3_out(pipe_mdwb_simd_1_m3_out), .r3_out(pipe_mdwb_simd_1_r3_out), .load_out(pipe_mdwb_simd_1_load_out),
    .rd_out(pipe_mdwb_simd_1_rd_out), .rwe_out(pipe_mdwb_simd_1_rwe_out));
  Multiplexer #(.width(8)) multiplexer_27 (
    .in0(pipe_mdwb_simd_1_r0_out), .in1(pipe_mdwb_simd_1_m0_out), .out(multiplexer_27_out),
    .sel(pipe_mdwb_simd_1_load_out));
  Multiplexer #(.width(8)) multiplexer_28 (
    .in0(pipe_mdwb_simd_1_r1_out), .in1(pipe_mdwb_simd_1_m1_out), .out(multiplexer_28_out),
    .sel(pipe_mdwb_simd_1_load_out));
  Multiplexer #(.width(8)) multiplexer_29 (
    .in0(pipe_mdwb_simd_1_r2_out), .in1(pipe_mdwb_simd_1_m2_out), .out(multiplexer_29_out),
    .sel(pipe_mdwb_simd_1_load_out));
  Multiplexer #(.width(8)) multiplexer_30 (
    .in0(pipe_mdwb_simd_1_r3_out), .in1(pipe_mdwb_simd_1_m3_out), .out(multiplexer_30_out),
    .sel(pipe_mdwb_simd_1_load_out));

  // Notes on the sheet:
  //   branch
  //   contents of MI (hex, n*v repeats v):
  //   d5 da df c8 cc 55 5a 33 49 21 36 79 9e d5 b4 c9 cd 55 31 59 20 39 71
  //   branch
  //   useImm
  //   imm
  //   ra
  //   rb
  //   store
  //   rwe
  //   load
  //   useImm
  //   rwe
  //   store
  //   load
  //   ra
  //   rb
  //   imm
endmodule

module idecoder (
  input  [3:0] opcode,
  output load,
  output rwe,
  output branch,
  output simd,
  output imm,
  output store
);

  wire or_1_out;

  and and_1 (imm, ~opcode[2], opcode[1]);  // AND_Gate
  and and_2 (store, opcode[0], ~opcode[1], ~opcode[2]);  // AND_Gate
  and and_3 (branch, opcode[0], opcode[1], opcode[2], ~opcode[3]);  // AND_Gate
  and and_4 (load, ~opcode[2], ~opcode[1], ~opcode[0]);  // AND_Gate
  or or_1 (or_1_out, store, branch);
  not not_1 (rwe, or_1_out);

  assign simd = opcode[3];
endmodule

module c_register_bank_seq (
  input  R,
  input  RC,
  input  [1:0] RA,
  input  [1:0] RB,
  input  FWE,
  input  [1:0] FRD,
  input  WE,
  input  [1:0] RD,
  input  [7:0] D,
  input  Clk,
  output Blk,
  output [7:0] DA,
  output [7:0] DB
);

  wire adder_1_cout, adder_2_cout, adder_3_cout, and_1_out, and_2_out, and_3_out, and_4_out,
       demultiplexer_1_out0, demultiplexer_1_out1, demultiplexer_1_out2, demultiplexer_1_out3,
       demultiplexer_2_out0, demultiplexer_2_out1, demultiplexer_2_out2, demultiplexer_2_out3,
       multiplexer_1_out, multiplexer_3_out, multiplexer_5_out, multiplexer_8_out, multiplexer_10_out,
       or_1_out, or_2_out, or_3_out, or_4_out, or_5_out, or_6_out, or_7_out;
  wire [1:0] adder_1_out, adder_2_out, adder_3_out, multiplexer_2_out, multiplexer_4_out, multiplexer_6_out,
       R1C_q, R2C_q, R3C_q;
  wire [7:0] R1_q, R2_q, R3_q;

  and and_1 (and_1_out, ~Blk, FWE);  // AND_Gate
  LED led_1 (.in(demultiplexer_1_out0));
  Demultiplexer #(.select(2)) demultiplexer_1 (
    .out0(demultiplexer_1_out0), .out1(demultiplexer_1_out1), .out2(demultiplexer_1_out2),
    .out3(demultiplexer_1_out3), .in(and_1_out), .sel(FRD));
  LED led_2 (.in(demultiplexer_2_out0));
  Demultiplexer #(.select(2)) demultiplexer_2 (
    .out0(demultiplexer_2_out0), .out1(demultiplexer_2_out1), .out2(demultiplexer_2_out2),
    .out3(demultiplexer_2_out3), .in(WE), .sel(RD));
  or or_1 (or_1_out, demultiplexer_2_out1, demultiplexer_1_out1);
  and and_2 (and_2_out, demultiplexer_2_out1, or_5_out);
  Multiplexer multiplexer_1 (.in0(1'b0), .in1(1'b1), .out(multiplexer_1_out), .sel(and_2_out));
  Adder #(.width(2)) adder_1 (
    .a(R1C_q), .b(multiplexer_2_out), .out(adder_1_out), .cin(multiplexer_1_out), .cout(adder_1_cout));
  Multiplexer #(.width(2)) multiplexer_2 (.in0(2'b01), .in1(2'b10), .out(multiplexer_2_out), .sel(and_2_out));
  LED led_3 (.in(adder_1_cout));
  or or_2 (or_2_out, demultiplexer_2_out2, demultiplexer_1_out2);
  and and_3 (and_3_out, demultiplexer_2_out2, or_6_out);
  Multiplexer multiplexer_3 (.in0(1'b0), .in1(1'b1), .out(multiplexer_3_out), .sel(and_3_out));
  Adder #(.width(2)) adder_2 (
    .a(R2C_q), .b(multiplexer_4_out), .out(adder_2_out), .cin(multiplexer_3_out), .cout(adder_2_cout));
  Multiplexer #(.width(2)) multiplexer_4 (.in0(2'b01), .in1(2'b10), .out(multiplexer_4_out), .sel(and_3_out));
  LED led_4 (.in(adder_2_cout));
  or or_3 (or_3_out, demultiplexer_2_out3, demultiplexer_1_out3);
  and and_4 (and_4_out, demultiplexer_2_out3, or_7_out);
  Multiplexer multiplexer_5 (.in0(1'b0), .in1(1'b1), .out(multiplexer_5_out), .sel(and_4_out));
  Adder #(.width(2)) adder_3 (
    .a(R3C_q), .b(multiplexer_6_out), .out(adder_3_out), .cin(multiplexer_5_out), .cout(adder_3_cout));
  Multiplexer #(.width(2)) multiplexer_6 (.in0(2'b01), .in1(2'b10), .out(multiplexer_6_out), .sel(and_4_out));
  LED led_5 (.in(adder_3_cout));
  Register R1 (.D(D), .en(demultiplexer_2_out1), .clk(Clk), .Q(R1_q), .clr(R));
  Register #(.width(2)) R1C (.D(adder_1_out), .en(or_1_out), .clk(Clk), .Q(R1C_q), .clr(or_4_out));
  Register R2 (.D(D), .en(demultiplexer_2_out2), .clk(Clk), .Q(R2_q), .clr(R));
  Register #(.width(2)) R2C (.D(adder_2_out), .en(or_2_out), .clk(Clk), .Q(R2C_q), .clr(or_4_out));
  Register R3 (.D(D), .en(demultiplexer_2_out3), .clk(Clk), .Q(R3_q), .clr(R));
  Register #(.width(2)) R3C (.D(adder_3_out), .en(or_3_out), .clk(Clk), .Q(R3C_q), .clr(or_4_out));
  or or_4 (or_4_out, R, RC);
  Multiplexer #(.select(2), .width(8)) multiplexer_7 (
    .in0({8{1'b0}}), .in1(R1_q), .in2(R2_q), .in3(R3_q), .out(DA), .sel(RA));
  or or_5 (or_5_out, R1C_q[0], R1C_q[1]);
  or or_6 (or_6_out, R2C_q[0], R2C_q[1]);
  or or_7 (or_7_out, R3C_q[0], R3C_q[1]);
  Multiplexer #(.select(2)) multiplexer_8 (
    .in0(1'b0), .in1(or_5_out), .in2(or_6_out), .in3(or_7_out), .out(multiplexer_8_out), .sel(RA));
  Multiplexer #(.select(2), .width(8)) multiplexer_9 (
    .in0({8{1'b0}}), .in1(R1_q), .in2(R2_q), .in3(R3_q), .out(DB), .sel(RB));
  or or_8 (Blk, multiplexer_8_out, multiplexer_10_out);
  Multiplexer #(.select(2)) multiplexer_10 (
    .in0(1'b0), .in1(or_5_out), .in2(or_6_out), .in3(or_7_out), .out(multiplexer_10_out), .sel(RB));
endmodule

module PIPE_REEX_seq (
  input  R,
  input  branch_in,
  input  [7:0] da_in,
  input  [7:0] db_in,
  input  store_in,
  input  [2:0] opcode_in,
  input  load_in,
  input  [1:0] rd_in,
  input  rwe_in,
  input  clk,
  output branch_out,
  output [7:0] da_out,
  output [7:0] db_out,
  output store_out,
  output [2:0] opcode_out,
  output load_out,
  output [1:0] rd_out,
  output rwe_out
);

  wire multiplexer_1_out, multiplexer_4_out, multiplexer_6_out, multiplexer_8_out;
  wire [1:0] multiplexer_7_out;
  wire [2:0] multiplexer_5_out;
  wire [7:0] multiplexer_2_out, multiplexer_3_out;

  Register #(.width(1)) branch (.D(multiplexer_1_out), .en(1'b1), .clk(clk), .Q(branch_out), .clr(1'b0));
  Multiplexer multiplexer_1 (.in0(branch_in), .in1(1'b0), .out(multiplexer_1_out), .sel(R));
  Register da (.D(multiplexer_2_out), .en(1'b1), .clk(clk), .Q(da_out), .clr(1'b0));
  Multiplexer #(.width(8)) multiplexer_2 (.in0(da_in), .in1({8{1'b0}}), .out(multiplexer_2_out), .sel(R));
  Register db (.D(multiplexer_3_out), .en(1'b1), .clk(clk), .Q(db_out), .clr(1'b0));
  Multiplexer #(.width(8)) multiplexer_3 (.in0(db_in), .in1({8{1'b0}}), .out(multiplexer_3_out), .sel(R));
  Register #(.width(1)) store (.D(multiplexer_4_out), .en(1'b1), .clk(clk), .Q(store_out), .clr(1'b0));
  Multiplexer multiplexer_4 (.in0(store_in), .in1(1'b0), .out(multiplexer_4_out), .sel(R));
  Register #(.width(3)) opcode (.D(multiplexer_5_out), .en(1'b1), .clk(clk), .Q(opcode_out), .clr(1'b0));
  Multiplexer #(.width(3)) multiplexer_5 (.in0(opcode_in), .in1(3'b110), .out(multiplexer_5_out), .sel(R));
  Register #(.width(1)) load (.D(multiplexer_6_out), .en(1'b1), .clk(clk), .Q(load_out), .clr(1'b0));
  Multiplexer multiplexer_6 (.in0(load_in), .in1(1'b0), .out(multiplexer_6_out), .sel(R));
  Register #(.width(2)) rd (.D(multiplexer_7_out), .en(1'b1), .clk(clk), .Q(rd_out), .clr(1'b0));
  Multiplexer #(.width(2)) multiplexer_7 (.in0(rd_in), .in1(2'b00), .out(multiplexer_7_out), .sel(R));
  Register #(.width(1)) rwe (.D(multiplexer_8_out), .en(1'b1), .clk(clk), .Q(rwe_out), .clr(1'b0));
  Multiplexer multiplexer_8 (.in0(rwe_in), .in1(1'b0), .out(multiplexer_8_out), .sel(R));
endmodule

module alu_seq (
  input  [7:0] da,
  input  [7:0] db,
  input  [2:0] opcode,
  output [7:0] R
);

  wire adder_1_cout, multiplexer_1_out, or_1_out;
  wire [7:0] adder_1_out, and_1_out, bit_extender_1_out, multiplexer_2_out, not_1_out;

  Multiplexer multiplexer_1 (.in0(1'b0), .in1(1'b1), .out(multiplexer_1_out), .sel(opcode[0]));
  Multiplexer #(.width(8)) multiplexer_2 (.in0(db), .in1(not_1_out), .out(multiplexer_2_out), .sel(opcode[0]));
  assign not_1_out = ~db;  // NOT_Gate not_1, 8 bits wide
  Adder adder_1 (.a(da), .b(multiplexer_2_out), .out(adder_1_out), .cin(multiplexer_1_out), .cout(adder_1_cout));
  LED led_1 (.in(adder_1_cout));
  or or_1 (or_1_out, da[7], da[6], da[5], da[4], da[3], da[2], da[1], da[0]);
  assign and_1_out = db & da;  // AND_Gate and_1, 8 bits wide
  assign bit_extender_1_out = {{7{1'b0}}, or_1_out};  // Bit_Extender bit_extender_1
  Multiplexer #(.select(3), .width(8)) multiplexer_3 (
    .in0(da), .in1(da), .in2({db[3:0], da[3:0]}), .in3({da[7:4], db[3:0]}), .in4(adder_1_out),
    .in5(adder_1_out), .in6(and_1_out), .in7(bit_extender_1_out), .out(R), .sel(opcode));
endmodule

module PIPE_EXMD_seq (
  input  R,
  input  branch_in,
  input  [7:0] da_in,
  input  [7:0] db_in,
  input  store_in,
  input  load_in,
  input  [1:0] rd_in,
  input  rwe_in,
  input  clk,
  output branch_out,
  output [7:0] da_out,
  output [7:0] db_out,
  output store_out,
  output load_out,
  output [1:0] rd_out,
  output rwe_out
);

  wire multiplexer_1_out, multiplexer_4_out, multiplexer_5_out, multiplexer_7_out;
  wire [1:0] multiplexer_6_out;
  wire [7:0] multiplexer_2_out, multiplexer_3_out;

  Register #(.width(1)) branch (.D(multiplexer_1_out), .en(1'b1), .clk(clk), .Q(branch_out), .clr(1'b0));
  Multiplexer multiplexer_1 (.in0(branch_in), .in1(1'b0), .out(multiplexer_1_out), .sel(R));
  Register da (.D(multiplexer_2_out), .en(1'b1), .clk(clk), .Q(da_out), .clr(1'b0));
  Multiplexer #(.width(8)) multiplexer_2 (.in0(da_in), .in1({8{1'b0}}), .out(multiplexer_2_out), .sel(R));
  Register db (.D(multiplexer_3_out), .en(1'b1), .clk(clk), .Q(db_out), .clr(1'b0));
  Multiplexer #(.width(8)) multiplexer_3 (.in0(db_in), .in1({8{1'b0}}), .out(multiplexer_3_out), .sel(R));
  Register #(.width(1)) store (.D(multiplexer_4_out), .en(1'b1), .clk(clk), .Q(store_out), .clr(1'b0));
  Multiplexer multiplexer_4 (.in0(store_in), .in1(1'b0), .out(multiplexer_4_out), .sel(R));
  Register #(.width(1)) load (.D(multiplexer_5_out), .en(1'b1), .clk(clk), .Q(load_out), .clr(1'b0));
  Multiplexer multiplexer_5 (.in0(load_in), .in1(1'b0), .out(multiplexer_5_out), .sel(R));
  Register #(.width(2)) rd (.D(multiplexer_6_out), .en(1'b1), .clk(clk), .Q(rd_out), .clr(1'b0));
  Multiplexer #(.width(2)) multiplexer_6 (.in0(rd_in), .in1(2'b00), .out(multiplexer_6_out), .sel(R));
  Register #(.width(1)) rwe (.D(multiplexer_7_out), .en(1'b1), .clk(clk), .Q(rwe_out), .clr(1'b0));
  Multiplexer multiplexer_7 (.in0(rwe_in), .in1(1'b0), .out(multiplexer_7_out), .sel(R));
endmodule

module PIPE_MDWB_seq (
  input  R,
  input  load_in,
  input  [7:0] rv_in,
  input  [7:0] md_in,
  input  [1:0] rd_in,
  input  rwe_in,
  input  clk,
  output load_out,
  output [7:0] rv_out,
  output [7:0] md_out,
  output [1:0] rd_out,
  output rwe_out
);

  wire multiplexer_1_out, multiplexer_5_out;
  wire [1:0] multiplexer_4_out;
  wire [7:0] multiplexer_2_out, multiplexer_3_out;

  Register #(.width(1)) load (.D(multiplexer_1_out), .en(1'b1), .clk(clk), .Q(load_out), .clr(1'b0));
  Multiplexer multiplexer_1 (.in0(load_in), .in1(1'b0), .out(multiplexer_1_out), .sel(R));
  Register rv (.D(multiplexer_2_out), .en(1'b1), .clk(clk), .Q(rv_out), .clr(1'b0));
  Multiplexer #(.width(8)) multiplexer_2 (.in0(rv_in), .in1({8{1'b0}}), .out(multiplexer_2_out), .sel(R));
  Register md (.D(multiplexer_3_out), .en(1'b1), .clk(clk), .Q(md_out), .clr(1'b0));
  Multiplexer #(.width(8)) multiplexer_3 (.in0(md_in), .in1({8{1'b0}}), .out(multiplexer_3_out), .sel(R));
  Register #(.width(2)) rd (.D(multiplexer_4_out), .en(1'b1), .clk(clk), .Q(rd_out), .clr(1'b0));
  Multiplexer #(.width(2)) multiplexer_4 (.in0(rd_in), .in1(2'b00), .out(multiplexer_4_out), .sel(R));
  Register #(.width(1)) rwe (.D(multiplexer_5_out), .en(1'b1), .clk(clk), .Q(rwe_out), .clr(1'b0));
  Multiplexer multiplexer_5 (.in0(rwe_in), .in1(1'b0), .out(multiplexer_5_out), .sel(R));
endmodule

module c_register_bank_simd (
  input  R,
  input  RC,
  input  [1:0] RA,
  input  [1:0] RB,
  input  FWE,
  input  [1:0] FRD,
  input  WE,
  input  [1:0] RD,
  input  Clk,
  input  [7:0] D0,
  input  [7:0] D1,
  input  [7:0] D2,
  input  [7:0] D3,
  output Blk,
  output [7:0] DA0,
  output [7:0] DA1,
  output [7:0] DA2,
  output [7:0] DA3,
  output [7:0] DB0,
  output [7:0] DB1,
  output [7:0] DB2,
  output [7:0] DB3
);

  wire adder_1_cout, adder_2_cout, adder_3_cout, and_1_out, and_2_out, and_3_out, and_4_out,
       demultiplexer_1_out0, demultiplexer_1_out1, demultiplexer_1_out2, demultiplexer_1_out3,
       demultiplexer_2_out0, demultiplexer_2_out1, demultiplexer_2_out2, demultiplexer_2_out3,
       multiplexer_1_out, multiplexer_3_out, multiplexer_5_out, multiplexer_7_out, multiplexer_8_out,
       or_1_out, or_2_out, or_3_out, or_4_out, or_6_out, or_7_out, or_8_out;
  wire [1:0] adder_1_out, adder_2_out, adder_3_out, multiplexer_2_out, multiplexer_4_out, multiplexer_6_out,
       R1C_q, R2C_q, R3C_q;
  wire [7:0] R10_q, R11_q, R12_q, R13_q, R20_q, R21_q, R22_q, R23_q, R30_q, R31_q, R32_q, R33_q;

  and and_1 (and_1_out, ~Blk, FWE);  // AND_Gate
  LED led_1 (.in(demultiplexer_1_out0));
  Demultiplexer #(.select(2)) demultiplexer_1 (
    .out0(demultiplexer_1_out0), .out1(demultiplexer_1_out1), .out2(demultiplexer_1_out2),
    .out3(demultiplexer_1_out3), .in(and_1_out), .sel(FRD));
  LED led_2 (.in(demultiplexer_2_out0));
  Demultiplexer #(.select(2)) demultiplexer_2 (
    .out0(demultiplexer_2_out0), .out1(demultiplexer_2_out1), .out2(demultiplexer_2_out2),
    .out3(demultiplexer_2_out3), .in(WE), .sel(RD));
  or or_1 (or_1_out, demultiplexer_2_out1, demultiplexer_1_out1);
  and and_2 (and_2_out, demultiplexer_2_out1, or_6_out);
  Multiplexer multiplexer_1 (.in0(1'b0), .in1(1'b1), .out(multiplexer_1_out), .sel(and_2_out));
  Adder #(.width(2)) adder_1 (
    .a(R1C_q), .b(multiplexer_2_out), .out(adder_1_out), .cin(multiplexer_1_out), .cout(adder_1_cout));
  Multiplexer #(.width(2)) multiplexer_2 (.in0(2'b01), .in1(2'b10), .out(multiplexer_2_out), .sel(and_2_out));
  LED led_3 (.in(adder_1_cout));
  or or_2 (or_2_out, demultiplexer_2_out2, demultiplexer_1_out2);
  and and_3 (and_3_out, demultiplexer_2_out2, or_7_out);
  Multiplexer multiplexer_3 (.in0(1'b0), .in1(1'b1), .out(multiplexer_3_out), .sel(and_3_out));
  Adder #(.width(2)) adder_2 (
    .a(R2C_q), .b(multiplexer_4_out), .out(adder_2_out), .cin(multiplexer_3_out), .cout(adder_2_cout));
  Multiplexer #(.width(2)) multiplexer_4 (.in0(2'b01), .in1(2'b10), .out(multiplexer_4_out), .sel(and_3_out));
  LED led_4 (.in(adder_2_cout));
  or or_3 (or_3_out, demultiplexer_2_out3, demultiplexer_1_out3);
  and and_4 (and_4_out, demultiplexer_2_out3, or_8_out);
  Multiplexer multiplexer_5 (.in0(1'b0), .in1(1'b1), .out(multiplexer_5_out), .sel(and_4_out));
  Adder #(.width(2)) adder_3 (
    .a(R3C_q), .b(multiplexer_6_out), .out(adder_3_out), .cin(multiplexer_5_out), .cout(adder_3_cout));
  Multiplexer #(.width(2)) multiplexer_6 (.in0(2'b01), .in1(2'b10), .out(multiplexer_6_out), .sel(and_4_out));
  LED led_5 (.in(adder_3_cout));
  Register #(.width(2)) R1C (.D(adder_1_out), .en(or_1_out), .clk(Clk), .Q(R1C_q), .clr(or_4_out));
  Register #(.width(2)) R2C (.D(adder_2_out), .en(or_2_out), .clk(Clk), .Q(R2C_q), .clr(or_4_out));
  Register #(.width(2)) R3C (.D(adder_3_out), .en(or_3_out), .clk(Clk), .Q(R3C_q), .clr(or_4_out));
  or or_4 (or_4_out, R, RC);
  Register R10 (.D(D0), .en(demultiplexer_2_out1), .clk(Clk), .Q(R10_q), .clr(R));
  Register R20 (.D(D0), .en(demultiplexer_2_out2), .clk(Clk), .Q(R20_q), .clr(R));
  Register R30 (.D(D0), .en(demultiplexer_2_out3), .clk(Clk), .Q(R30_q), .clr(R));
  Register R11 (.D(D1), .en(demultiplexer_2_out1), .clk(Clk), .Q(R11_q), .clr(R));
  Register R21 (.D(D1), .en(demultiplexer_2_out2), .clk(Clk), .Q(R21_q), .clr(R));
  Register R31 (.D(D1), .en(demultiplexer_2_out3), .clk(Clk), .Q(R31_q), .clr(R));
  Register R12 (.D(D2), .en(demultiplexer_2_out1), .clk(Clk), .Q(R12_q), .clr(R));
  Register R22 (.D(D2), .en(demultiplexer_2_out2), .clk(Clk), .Q(R22_q), .clr(R));
  Register R32 (.D(D2), .en(demultiplexer_2_out3), .clk(Clk), .Q(R32_q), .clr(R));
  Register R13 (.D(D3), .en(demultiplexer_2_out1), .clk(Clk), .Q(R13_q), .clr(R));
  Register R23 (.D(D3), .en(demultiplexer_2_out2), .clk(Clk), .Q(R23_q), .clr(R));
  Register R33 (.D(D3), .en(demultiplexer_2_out3), .clk(Clk), .Q(R33_q), .clr(R));
  or or_5 (Blk, multiplexer_7_out, multiplexer_8_out);
  Multiplexer #(.select(2)) multiplexer_7 (
    .in0(1'b0), .in1(or_6_out), .in2(or_7_out), .in3(or_8_out), .out(multiplexer_7_out), .sel(RA));
  or or_6 (or_6_out, R1C_q[0], R1C_q[1]);
  or or_7 (or_7_out, R2C_q[0], R2C_q[1]);
  or or_8 (or_8_out, R3C_q[0], R3C_q[1]);
  Multiplexer #(.select(2)) multiplexer_8 (
    .in0(1'b0), .in1(or_6_out), .in2(or_7_out), .in3(or_8_out), .out(multiplexer_8_out), .sel(RB));
  Multiplexer #(.select(2), .width(8)) multiplexer_9 (
    .in0({8{1'b0}}), .in1(R10_q), .in2(R20_q), .in3(R30_q), .out(DA0), .sel(RA));
  Multiplexer #(.select(2), .width(8)) multiplexer_10 (
    .in0(8'h1), .in1(R11_q), .in2(R21_q), .in3(R31_q), .out(DA1), .sel(RA));
  Multiplexer #(.select(2), .width(8)) multiplexer_11 (
    .in0(8'h2), .in1(R12_q), .in2(R22_q), .in3(R32_q), .out(DA2), .sel(RA));
  Multiplexer #(.select(2), .width(8)) multiplexer_12 (
    .in0(8'h3), .in1(R13_q), .in2(R23_q), .in3(R33_q), .out(DA3), .sel(RA));
  Multiplexer #(.select(2), .width(8)) multiplexer_13 (
    .in0({8{1'b0}}), .in1(R10_q), .in2(R20_q), .in3(R30_q), .out(DB0), .sel(RB));
  Multiplexer #(.select(2), .width(8)) multiplexer_14 (
    .in0(8'h1), .in1(R11_q), .in2(R21_q), .in3(R31_q), .out(DB1), .sel(RB));
  Multiplexer #(.select(2), .width(8)) multiplexer_15 (
    .in0(8'h2), .in1(R12_q), .in2(R22_q), .in3(R32_q), .out(DB2), .sel(RB));
  Multiplexer #(.select(2), .width(8)) multiplexer_16 (
    .in0(8'h3), .in1(R13_q), .in2(R23_q), .in3(R33_q), .out(DB3), .sel(RB));
endmodule

module PIPE_REEX_simd (
  input  R,
  input  [7:0] da0_in,
  input  [7:0] da1_in,
  input  [7:0] da2_in,
  input  [7:0] da3_in,
  input  [7:0] db0_in,
  input  [7:0] db1_in,
  input  [7:0] db2_in,
  input  [7:0] db3_in,
  input  store_in,
  input  [2:0] opcode_in,
  input  load_in,
  input  [1:0] rd_in,
  input  rwe_in,
  input  clk,
  output [7:0] da0_out,
  output [7:0] da1_out,
  output [7:0] da2_out,
  output [7:0] da3_out,
  output [7:0] db0_out,
  output [7:0] db1_out,
  output [7:0] db2_out,
  output [7:0] db3_out,
  output store_out,
  output [2:0] opcode_out,
  output load_out,
  output [1:0] rd_out,
  output rwe_out
);

  wire multiplexer_9_out, multiplexer_11_out, multiplexer_13_out;
  wire [1:0] multiplexer_12_out;
  wire [2:0] multiplexer_10_out;
  wire [7:0] multiplexer_1_out, multiplexer_2_out, multiplexer_3_out, multiplexer_4_out, multiplexer_5_out,
       multiplexer_6_out, multiplexer_7_out, multiplexer_8_out;

  Multiplexer #(.width(8)) multiplexer_1 (.in0(da0_in), .in1({8{1'b0}}), .out(multiplexer_1_out), .sel(R));
  Multiplexer #(.width(8)) multiplexer_2 (.in0(da1_in), .in1({8{1'b0}}), .out(multiplexer_2_out), .sel(R));
  Multiplexer #(.width(8)) multiplexer_3 (.in0(da2_in), .in1({8{1'b0}}), .out(multiplexer_3_out), .sel(R));
  Multiplexer #(.width(8)) multiplexer_4 (.in0(da3_in), .in1({8{1'b0}}), .out(multiplexer_4_out), .sel(R));
  Multiplexer #(.width(8)) multiplexer_5 (.in0(db0_in), .in1({8{1'b0}}), .out(multiplexer_5_out), .sel(R));
  Multiplexer #(.width(8)) multiplexer_6 (.in0(db1_in), .in1({8{1'b0}}), .out(multiplexer_6_out), .sel(R));
  Multiplexer #(.width(8)) multiplexer_7 (.in0(db2_in), .in1({8{1'b0}}), .out(multiplexer_7_out), .sel(R));
  Multiplexer #(.width(8)) multiplexer_8 (.in0(db3_in), .in1({8{1'b0}}), .out(multiplexer_8_out), .sel(R));
  Multiplexer multiplexer_9 (.in0(store_in), .in1(1'b0), .out(multiplexer_9_out), .sel(R));
  Multiplexer #(.width(3)) multiplexer_10 (.in0(opcode_in), .in1(3'b110), .out(multiplexer_10_out), .sel(R));
  Multiplexer multiplexer_11 (.in0(load_in), .in1(1'b0), .out(multiplexer_11_out), .sel(R));
  Multiplexer #(.width(2)) multiplexer_12 (.in0(rd_in), .in1(2'b00), .out(multiplexer_12_out), .sel(R));
  Multiplexer multiplexer_13 (.in0(rwe_in), .in1(1'b0), .out(multiplexer_13_out), .sel(R));
  Register da0 (.D(multiplexer_1_out), .en(1'b1), .clk(clk), .Q(da0_out), .clr(1'b0));
  Register da1 (.D(multiplexer_2_out), .en(1'b1), .clk(clk), .Q(da1_out), .clr(1'b0));
  Register da2 (.D(multiplexer_3_out), .en(1'b1), .clk(clk), .Q(da2_out), .clr(1'b0));
  Register da3 (.D(multiplexer_4_out), .en(1'b1), .clk(clk), .Q(da3_out), .clr(1'b0));
  Register db0 (.D(multiplexer_5_out), .en(1'b1), .clk(clk), .Q(db0_out), .clr(1'b0));
  Register db1 (.D(multiplexer_6_out), .en(1'b1), .clk(clk), .Q(db1_out), .clr(1'b0));
  Register db2 (.D(multiplexer_7_out), .en(1'b1), .clk(clk), .Q(db2_out), .clr(1'b0));
  Register db3 (.D(multiplexer_8_out), .en(1'b1), .clk(clk), .Q(db3_out), .clr(1'b0));
  Register #(.width(1)) store (.D(multiplexer_9_out), .en(1'b1), .clk(clk), .Q(store_out), .clr(1'b0));
  Register #(.width(3)) opcode (.D(multiplexer_10_out), .en(1'b1), .clk(clk), .Q(opcode_out), .clr(1'b0));
  Register #(.width(1)) load (.D(multiplexer_11_out), .en(1'b1), .clk(clk), .Q(load_out), .clr(1'b0));
  Register #(.width(2)) rd (.D(multiplexer_12_out), .en(1'b1), .clk(clk), .Q(rd_out), .clr(1'b0));
  Register #(.width(1)) rwe (.D(multiplexer_13_out), .en(1'b1), .clk(clk), .Q(rwe_out), .clr(1'b0));
endmodule

module alu_simd (
  input  [7:0] da,
  input  [7:0] db,
  input  [2:0] opcode,
  output [7:0] R
);

  wire adder_1_cout, multiplexer_1_out;
  wire [7:0] adder_1_out, and_1_out, multiplexer_2_out, not_1_out, or_1_out;

  Multiplexer multiplexer_1 (.in0(1'b0), .in1(1'b1), .out(multiplexer_1_out), .sel(opcode[0]));
  Multiplexer #(.width(8)) multiplexer_2 (.in0(db), .in1(not_1_out), .out(multiplexer_2_out), .sel(opcode[0]));
  assign not_1_out = ~db;  // NOT_Gate not_1, 8 bits wide
  Adder adder_1 (.a(da), .b(multiplexer_2_out), .out(adder_1_out), .cin(multiplexer_1_out), .cout(adder_1_cout));
  LED led_1 (.in(adder_1_cout));
  assign and_1_out = db & da;  // AND_Gate and_1, 8 bits wide
  assign or_1_out = db | da;  // OR_Gate or_1, 8 bits wide
  Multiplexer #(.select(3), .width(8)) multiplexer_3 (
    .in0(da), .in1(da), .in2({db[3:0], da[3:0]}), .in3({da[7:4], db[3:0]}), .in4(adder_1_out),
    .in5(adder_1_out), .in6(and_1_out), .in7(or_1_out), .out(R), .sel(opcode));
endmodule

module PIPE_EXMD_simd (
  input  R,
  input  [7:0] da0_in,
  input  [7:0] da1_in,
  input  [7:0] da2_in,
  input  [7:0] da3_in,
  input  [7:0] db0_in,
  input  [7:0] db1_in,
  input  [7:0] db2_in,
  input  [7:0] db3_in,
  input  store_in,
  input  load_in,
  input  [1:0] rd_in,
  input  rwe_in,
  input  clk,
  output [7:0] da0_out,
  output [7:0] da1_out,
  output [7:0] da2_out,
  output [7:0] da3_out,
  output [7:0] db0_out,
  output [7:0] db1_out,
  output [7:0] db2_out,
  output [7:0] db3_out,
  output store_out,
  output load_out,
  output [1:0] rd_out,
  output rwe_out
);

  wire multiplexer_9_out, multiplexer_10_out, multiplexer_12_out;
  wire [1:0] multiplexer_11_out;
  wire [7:0] multiplexer_1_out, multiplexer_2_out, multiplexer_3_out, multiplexer_4_out, multiplexer_5_out,
       multiplexer_6_out, multiplexer_7_out, multiplexer_8_out;

  Multiplexer #(.width(8)) multiplexer_1 (.in0(da0_in), .in1({8{1'b0}}), .out(multiplexer_1_out), .sel(R));
  Multiplexer #(.width(8)) multiplexer_2 (.in0(da1_in), .in1({8{1'b0}}), .out(multiplexer_2_out), .sel(R));
  Multiplexer #(.width(8)) multiplexer_3 (.in0(da2_in), .in1({8{1'b0}}), .out(multiplexer_3_out), .sel(R));
  Multiplexer #(.width(8)) multiplexer_4 (.in0(da3_in), .in1({8{1'b0}}), .out(multiplexer_4_out), .sel(R));
  Multiplexer #(.width(8)) multiplexer_5 (.in0(db0_in), .in1({8{1'b0}}), .out(multiplexer_5_out), .sel(R));
  Multiplexer #(.width(8)) multiplexer_6 (.in0(db1_in), .in1({8{1'b0}}), .out(multiplexer_6_out), .sel(R));
  Multiplexer #(.width(8)) multiplexer_7 (.in0(db2_in), .in1({8{1'b0}}), .out(multiplexer_7_out), .sel(R));
  Multiplexer #(.width(8)) multiplexer_8 (.in0(db3_in), .in1({8{1'b0}}), .out(multiplexer_8_out), .sel(R));
  Multiplexer multiplexer_9 (.in0(store_in), .in1(1'b0), .out(multiplexer_9_out), .sel(R));
  Multiplexer multiplexer_10 (.in0(load_in), .in1(1'b0), .out(multiplexer_10_out), .sel(R));
  Multiplexer #(.width(2)) multiplexer_11 (.in0(rd_in), .in1(2'b00), .out(multiplexer_11_out), .sel(R));
  Multiplexer multiplexer_12 (.in0(rwe_in), .in1(1'b0), .out(multiplexer_12_out), .sel(R));
  Register da0 (.D(multiplexer_1_out), .en(1'b1), .clk(clk), .Q(da0_out), .clr(1'b0));
  Register da1 (.D(multiplexer_2_out), .en(1'b1), .clk(clk), .Q(da1_out), .clr(1'b0));
  Register da2 (.D(multiplexer_3_out), .en(1'b1), .clk(clk), .Q(da2_out), .clr(1'b0));
  Register da3 (.D(multiplexer_4_out), .en(1'b1), .clk(clk), .Q(da3_out), .clr(1'b0));
  Register db0 (.D(multiplexer_5_out), .en(1'b1), .clk(clk), .Q(db0_out), .clr(1'b0));
  Register db1 (.D(multiplexer_6_out), .en(1'b1), .clk(clk), .Q(db1_out), .clr(1'b0));
  Register db2 (.D(multiplexer_7_out), .en(1'b1), .clk(clk), .Q(db2_out), .clr(1'b0));
  Register db3 (.D(multiplexer_8_out), .en(1'b1), .clk(clk), .Q(db3_out), .clr(1'b0));
  Register #(.width(1)) store (.D(multiplexer_9_out), .en(1'b1), .clk(clk), .Q(store_out), .clr(1'b0));
  Register #(.width(1)) load (.D(multiplexer_10_out), .en(1'b1), .clk(clk), .Q(load_out), .clr(1'b0));
  Register #(.width(2)) rd (.D(multiplexer_11_out), .en(1'b1), .clk(clk), .Q(rd_out), .clr(1'b0));
  Register #(.width(1)) rwe (.D(multiplexer_12_out), .en(1'b1), .clk(clk), .Q(rwe_out), .clr(1'b0));
endmodule

module PIPE_MDWB_simd (
  input  R,
  input  [7:0] m0_in,
  input  [7:0] r0_in,
  input  [7:0] m1_in,
  input  [7:0] r1_in,
  input  [7:0] m2_in,
  input  [7:0] r2_in,
  input  [7:0] m3_in,
  input  [7:0] r3_in,
  input  load_in,
  input  [1:0] rd_in,
  input  rwe_in,
  input  clk,
  output [7:0] m0_out,
  output [7:0] r0_out,
  output [7:0] m1_out,
  output [7:0] r1_out,
  output [7:0] m2_out,
  output [7:0] r2_out,
  output [7:0] m3_out,
  output [7:0] r3_out,
  output load_out,
  output [1:0] rd_out,
  output rwe_out
);

  wire multiplexer_9_out, multiplexer_11_out;
  wire [1:0] multiplexer_10_out;
  wire [7:0] multiplexer_1_out, multiplexer_2_out, multiplexer_3_out, multiplexer_4_out, multiplexer_5_out,
       multiplexer_6_out, multiplexer_7_out, multiplexer_8_out;

  Multiplexer #(.width(8)) multiplexer_1 (.in0(m0_in), .in1({8{1'b0}}), .out(multiplexer_1_out), .sel(R));
  Multiplexer #(.width(8)) multiplexer_2 (.in0(r0_in), .in1({8{1'b0}}), .out(multiplexer_2_out), .sel(R));
  Multiplexer #(.width(8)) multiplexer_3 (.in0(m1_in), .in1({8{1'b0}}), .out(multiplexer_3_out), .sel(R));
  Multiplexer #(.width(8)) multiplexer_4 (.in0(r1_in), .in1({8{1'b0}}), .out(multiplexer_4_out), .sel(R));
  Multiplexer #(.width(8)) multiplexer_5 (.in0(m2_in), .in1({8{1'b0}}), .out(multiplexer_5_out), .sel(R));
  Multiplexer #(.width(8)) multiplexer_6 (.in0(r2_in), .in1({8{1'b0}}), .out(multiplexer_6_out), .sel(R));
  Multiplexer #(.width(8)) multiplexer_7 (.in0(m3_in), .in1({8{1'b0}}), .out(multiplexer_7_out), .sel(R));
  Multiplexer #(.width(8)) multiplexer_8 (.in0(r3_in), .in1({8{1'b0}}), .out(multiplexer_8_out), .sel(R));
  Multiplexer multiplexer_9 (.in0(load_in), .in1(1'b0), .out(multiplexer_9_out), .sel(R));
  Multiplexer #(.width(2)) multiplexer_10 (.in0(rd_in), .in1(2'b00), .out(multiplexer_10_out), .sel(R));
  Multiplexer multiplexer_11 (.in0(rwe_in), .in1(1'b0), .out(multiplexer_11_out), .sel(R));
  Register m0 (.D(multiplexer_1_out), .en(1'b1), .clk(clk), .Q(m0_out), .clr(1'b0));
  Register r0 (.D(multiplexer_2_out), .en(1'b1), .clk(clk), .Q(r0_out), .clr(1'b0));
  Register m1 (.D(multiplexer_3_out), .en(1'b1), .clk(clk), .Q(m1_out), .clr(1'b0));
  Register r1 (.D(multiplexer_4_out), .en(1'b1), .clk(clk), .Q(r1_out), .clr(1'b0));
  Register m2 (.D(multiplexer_5_out), .en(1'b1), .clk(clk), .Q(m2_out), .clr(1'b0));
  Register r2 (.D(multiplexer_6_out), .en(1'b1), .clk(clk), .Q(r2_out), .clr(1'b0));
  Register m3 (.D(multiplexer_7_out), .en(1'b1), .clk(clk), .Q(m3_out), .clr(1'b0));
  Register r3 (.D(multiplexer_8_out), .en(1'b1), .clk(clk), .Q(r3_out), .clr(1'b0));
  Register #(.width(1)) load (.D(multiplexer_9_out), .en(1'b1), .clk(clk), .Q(load_out), .clr(1'b0));
  Register #(.width(2)) rd (.D(multiplexer_10_out), .en(1'b1), .clk(clk), .Q(rd_out), .clr(1'b0));
  Register #(.width(1)) rwe (.D(multiplexer_11_out), .en(1'b1), .clk(clk), .Q(rwe_out), .clr(1'b0));
endmodule
