// Logisim project sagui.circ as structural Verilog: 7 circuits, main circuit main
module main (
);

  wire adder_1_cout, adder_2_cout, and_1_out, and_2_out, and_3_out, c_register_bank_1_blk, clock_1_out,
       idecoder_1_jmp, idecoder_1_jmpz, idecoder_1_mwe, idecoder_1_rwe, idecoder_1_useimm, not_1_out,
       or_1_out, or_2_out, or_3_out, pipe_exmd_1_branch_out, pipe_exmd_1_load_out, pipe_exmd_1_mwe_out,
       pipe_exmd_1_rwe_out, pipe_mdwb_1_load_out, pipe_mdwb_1_we_out, pipe_reex_1_jmp_out,
       pipe_reex_1_jmpz_out, pipe_reex_1_mwe_out, pipe_reex_1_rwe_out, pipe_reex_1_useimm_out,
       Reset_Pipeline_out;
  wire [1:0] multiplexer_2_out, multiplexer_3_out, pipe_exmd_1_rd_out, pipe_mdwb_1_rd_out, pipe_reex_1_rd_out;
  wire [3:0] pipe_reex_1_opcode_out;
  wire [7:0] adder_1_out, adder_2_out, alu_1_r, bit_extender_1_out, c_register_bank_1_da,
       c_register_bank_1_db, MD_dout, MI_data, multiplexer_1_out, multiplexer_4_out, multiplexer_5_out,
       multiplexer_6_out, multiplexer_7_out, PC_q, pipe_exmd_1_da_out, pipe_exmd_1_pc_out,
       pipe_exmd_1_res_out, pipe_mdwb_1_mem_out, pipe_mdwb_1_res_out, pipe_reex_1_da_out, pipe_reex_1_db_out,
       pipe_reex_1_imm_out, pipe_reex_1_pc_out;

  LED led_1 (.in(adder_1_cout));
  Register PC (.D(multiplexer_1_out), .en(not_1_out), .clk(clock_1_out), .Q(PC_q), .clr(Reset_Pipeline_out));
  Adder adder_1 (.a(PC_q), .b(8'h1), .out(adder_1_out), .cin(1'b0), .cout(adder_1_cout));
  Multiplexer #(.width(8)) multiplexer_1 (
    .in0(adder_1_out), .in1(pipe_exmd_1_pc_out), .out(multiplexer_1_out), .sel(pipe_exmd_1_branch_out));
  not not_1 (not_1_out, and_1_out);
  and and_1 (and_1_out, ~pipe_exmd_1_branch_out, c_register_bank_1_blk);  // AND_Gate
  ROM MI (.addr(PC_q), .data(MI_data));
  // Probe on MI_data
  Button Reset_Pipeline (.out(Reset_Pipeline_out));
  or or_1 (or_1_out, Reset_Pipeline_out, pipe_exmd_1_branch_out);
  Clock clock_1 (.out(clock_1_out));
  // Probe on MI_data[7:4]
  idecoder idecoder_1 (
    .opcode(MI_data[7:4]), .jmpz(idecoder_1_jmpz), .jmp(idecoder_1_jmp), .useImm(idecoder_1_useimm),
    .RWE(idecoder_1_rwe), .MWE(idecoder_1_mwe));
  // Probe on MI_data[7:4]
  // Probe on multiplexer_3_out
  // Probe on multiplexer_2_out
  Multiplexer #(.width(2)) multiplexer_2 (
    .in0(MI_data[3:2]), .in1(2'b00), .out(multiplexer_2_out), .sel(idecoder_1_useimm));
  Multiplexer #(.width(2)) multiplexer_3 (
    .in0(MI_data[1:0]), .in1(2'b00), .out(multiplexer_3_out), .sel(idecoder_1_useimm));
  assign bit_extender_1_out = {{4{MI_data[3]}}, MI_data[3:0]};  // Bit_Extender bit_extender_1
  c_register_bank c_register_bank_1 (
    .R(Reset_Pipeline_out), .RC(pipe_exmd_1_branch_out), .RA(multiplexer_2_out), .RB(multiplexer_3_out),
    .FWE(idecoder_1_rwe), .FRD(multiplexer_2_out), .WE(pipe_mdwb_1_we_out), .RD(pipe_mdwb_1_rd_out),
    .D(multiplexer_7_out), .Clk(clock_1_out), .Blk(c_register_bank_1_blk), .DA(c_register_bank_1_da),
    .DB(c_register_bank_1_db));
  or or_2 (or_2_out, or_1_out, c_register_bank_1_blk);
  // Probe on bit_extender_1_out
  // Probe on multiplexer_4_out
  // Probe on c_register_bank_1_da
  Multiplexer #(.width(8)) multiplexer_4 (
    .in0(c_register_bank_1_db), .in1({8{1'b0}}), .out(multiplexer_4_out), .sel(idecoder_1_useimm));
  PIPE_REEX pipe_reex_1 (
    .Imm_in(bit_extender_1_out), .DA_in(c_register_bank_1_da), .DB_in(multiplexer_4_out),
    .jmpz_in(idecoder_1_jmpz), .jmp_in(idecoder_1_jmp), .useImm_in(idecoder_1_useimm),
    .RWE_in(idecoder_1_rwe), .MWE_in(idecoder_1_mwe), .opcode_in(MI_data[7:4]), .PC_in(PC_q),
    .RD_in(multiplexer_2_out), .Clk(clock_1_out), .R(or_2_out), .Imm_out(pipe_reex_1_imm_out),
    .DA_out(pipe_reex_1_da_out), .DB_out(pipe_reex_1_db_out), .jmpz_out(pipe_reex_1_jmpz_out),
    .jmp_out(pipe_reex_1_jmp_out), .useImm_out(pipe_reex_1_useimm_out), .RWE_out(pipe_reex_1_rwe_out),
    .MWE_out(pipe_reex_1_mwe_out), .opcode_out(pipe_reex_1_opcode_out), .PC_out(pipe_reex_1_pc_out),
    .RD_out(pipe_reex_1_rd_out));
  // Probe on pipe_reex_1_da_out
  // Probe on pipe_reex_1_db_out
  // Probe on pipe_reex_1_opcode_out
  Adder adder_2 (.a(pipe_reex_1_pc_out), .b(pipe_reex_1_imm_out), .out(adder_2_out), .cin(1'b0), .cout(adder_2_cout));
  LED led_2 (.in(adder_2_cout));
  Multiplexer #(.width(8)) multiplexer_5 (
    .in0(pipe_reex_1_db_out), .in1(pipe_reex_1_imm_out), .out(multiplexer_5_out), .sel(pipe_reex_1_useimm_out));
  Multiplexer #(.width(8)) multiplexer_6 (
    .in0(pipe_reex_1_db_out), .in1(adder_2_out), .out(multiplexer_6_out), .sel(pipe_reex_1_useimm_out));
  and and_2 (and_2_out, ~pipe_reex_1_opcode_out[0], ~pipe_reex_1_opcode_out[1], pipe_reex_1_opcode_out[2], ~pipe_reex_1_opcode_out[3]);  // AND_Gate
  // Probe on alu_1_r
  alu alu_1 (.A(pipe_reex_1_da_out), .B(multiplexer_5_out), .opcode(pipe_reex_1_opcode_out), .R(alu_1_r));
  or or_3 (or_3_out, pipe_reex_1_jmp_out, and_3_out);
  and and_3 (and_3_out, pipe_reex_1_jmpz_out, ~alu_1_r[0]);  // AND_Gate
  RAM #(.asyncread("true"), .trigger("falling"), .\type ("nonvolatile")) MD (
    .addr(pipe_exmd_1_res_out), .we(pipe_exmd_1_mwe_out), .oe(1'b1), .clk(clock_1_out),
    .din(pipe_exmd_1_da_out), .dout(MD_dout));
  PIPE_EXMD pipe_exmd_1 (
    .DA_in(pipe_reex_1_da_out), .Branch_in(or_3_out), .Res_in(alu_1_r), .Load_in(and_2_out),
    .RWE_in(pipe_reex_1_rwe_out), .MWE_in(pipe_reex_1_mwe_out), .PC_in(multiplexer_6_out),
    .RD_in(pipe_reex_1_rd_out), .R(or_1_out), .Clk(clock_1_out), .DA_out(pipe_exmd_1_da_out),
    .Branch_out(pipe_exmd_1_branch_out), .Res_out(pipe_exmd_1_res_out), .Load_out(pipe_exmd_1_load_out),
    .RWE_out(pipe_exmd_1_rwe_out), .MWE_out(pipe_exmd_1_mwe_out), .PC_out(pipe_exmd_1_pc_out),
    .RD_out(pipe_exmd_1_rd_out));
  // Probe on pipe_exmd_1_res_out
  // Probe on MD_dout
  PIPE_MDWB pipe_mdwb_1 (
    .Res_in(pipe_exmd_1_res_out), .Mem_in(MD_dout), .Load_in(pipe_exmd_1_load_out),
    .RD_in(pipe_exmd_1_rd_out), .WE_in(pipe_exmd_1_rwe_out), .Clk(clock_1_out), .R(Reset_Pipeline_out),
    .Res_out(pipe_mdwb_1_res_out), .Mem_out(pipe_mdwb_1_mem_out), .Load_out(pipe_mdwb_1_load_out),
    .RD_out(pipe_mdwb_1_rd_out), .WE_out(pipe_mdwb_1_we_out));
  Multiplexer #(.width(8)) multiplexer_7 (
    .in0(pipe_mdwb_1_res_out), .in1(pipe_mdwb_1_mem_out), .out(multiplexer_7_out), .sel(pipe_mdwb_1_load_out));
  // Probe on multiplexer_7_out

  // Notes on the sheet:
  //   contents of MI (hex, n*v repeats v):
  //   89 71 68 a0 8a 6c 88 71 c a0 46 8a 98 42 94 56 a0 89 a8 81 ac 86 70 20 60 1 2 3 4 5 6 7 8 9 a 1 2 3
  //   4 5 6 7 8 9 a
endmodule

module idecoder (
  input  [3:0] opcode,
  output jmpz,
  output jmp,
  output useImm,
  output RWE,
  output MWE
);

  wire and_1_out, and_2_out, and_3_out, and_4_out, and_7_out, or_1_out;

  and and_1 (and_1_out, opcode[0], ~opcode[3]);  // AND_Gate
  and and_2 (and_2_out, opcode[2], opcode[1]);
  or or_1 (or_1_out, and_2_out, ~opcode[2]);  // OR_Gate
  and and_3 (and_3_out, ~opcode[0], ~opcode[1], ~opcode[2], opcode[3]);  // AND_Gate
  and and_4 (and_4_out, or_1_out, and_1_out);
  and and_5 (jmp, ~opcode[3], ~opcode[2], opcode[1]);  // AND_Gate
  and and_6 (jmpz, ~opcode[3], ~opcode[2], ~opcode[1]);  // AND_Gate
  or or_2 (useImm, and_3_out, and_4_out);
  and and_7 (and_7_out, ~opcode[3], ~opcode[2]);  // AND_Gate
  and and_8 (MWE, ~opcode[3], opcode[2], ~opcode[1], opcode[0]);  // AND_Gate
  and and_9 (RWE, ~MWE, ~and_7_out);  // AND_Gate
endmodule

module PIPE_REEX (
  input  [7:0] Imm_in,
  input  [7:0] DA_in,
  input  [7:0] DB_in,
  input  jmpz_in,
  input  jmp_in,
  input  useImm_in,
  input  RWE_in,
  input  MWE_in,
  input  [3:0] opcode_in,
  input  [7:0] PC_in,
  input  [1:0] RD_in,
  input  Clk,
  input  R,
  output [7:0] Imm_out,
  output [7:0] DA_out,
  output [7:0] DB_out,
  output jmpz_out,
  output jmp_out,
  output useImm_out,
  output RWE_out,
  output MWE_out,
  output [3:0] opcode_out,
  output [7:0] PC_out,
  output [1:0] RD_out
);

  wire multiplexer_4_out, multiplexer_5_out, multiplexer_6_out, multiplexer_7_out, multiplexer_8_out;
  wire [3:0] multiplexer_9_out;
  wire [7:0] multiplexer_1_out, multiplexer_2_out, multiplexer_3_out, multiplexer_10_out;

  Register Imm (.D(multiplexer_1_out), .en(1'b1), .clk(Clk), .Q(Imm_out), .clr(1'b0));
  Multiplexer #(.width(8)) multiplexer_1 (.in0(Imm_in), .in1({8{1'b0}}), .out(multiplexer_1_out), .sel(R));
  Register DA (.D(multiplexer_2_out), .en(1'b1), .clk(Clk), .Q(DA_out), .clr(1'b0));
  Multiplexer #(.width(8)) multiplexer_2 (.in0(DA_in), .in1({8{1'b0}}), .out(multiplexer_2_out), .sel(R));
  Register DB (.D(multiplexer_3_out), .en(1'b1), .clk(Clk), .Q(DB_out), .clr(1'b0));
  Multiplexer #(.width(8)) multiplexer_3 (.in0(DB_in), .in1({8{1'b0}}), .out(multiplexer_3_out), .sel(R));
  Register #(.width(1)) jmpz (.D(multiplexer_4_out), .en(1'b1), .clk(Clk), .Q(jmpz_out), .clr(1'b0));
  Multiplexer multiplexer_4 (.in0(jmpz_in), .in1(1'b0), .out(multiplexer_4_out), .sel(R));
  Register #(.width(1)) jmp (.D(multiplexer_5_out), .en(1'b1), .clk(Clk), .Q(jmp_out), .clr(1'b0));
  Multiplexer multiplexer_5 (.in0(jmp_in), .in1(1'b0), .out(multiplexer_5_out), .sel(R));
  Register #(.width(1)) useImm (.D(multiplexer_6_out), .en(1'b1), .clk(Clk), .Q(useImm_out), .clr(1'b0));
  Multiplexer multiplexer_6 (.in0(useImm_in), .in1(1'b0), .out(multiplexer_6_out), .sel(R));
  Register #(.width(1)) RWE (.D(multiplexer_7_out), .en(1'b1), .clk(Clk), .Q(RWE_out), .clr(1'b0));
  Multiplexer multiplexer_7 (.in0(RWE_in), .in1(1'b0), .out(multiplexer_7_out), .sel(R));
  Register #(.width(1)) MWE (.D(multiplexer_8_out), .en(1'b1), .clk(Clk), .Q(MWE_out), .clr(1'b0));
  Multiplexer multiplexer_8 (.in0(MWE_in), .in1(1'b0), .out(multiplexer_8_out), .sel(R));
  Register #(.width(4)) opcode (.D(multiplexer_9_out), .en(1'b1), .clk(Clk), .Q(opcode_out), .clr(1'b0));
  Multiplexer #(.width(4)) multiplexer_9 (.in0(opcode_in), .in1(4'b1111), .out(multiplexer_9_out), .sel(R));
  Register PC (.D(multiplexer_10_out), .en(1'b1), .clk(Clk), .Q(PC_out), .clr(1'b0));
  Multiplexer #(.width(8)) multiplexer_10 (.in0(PC_in), .in1({8{1'b0}}), .out(multiplexer_10_out), .sel(R));
  Register #(.width(2)) RD (.D(RD_in), .en(1'b1), .clk(Clk), .Q(RD_out), .clr(1'b0));
endmodule

module alu (
  input  [7:0] A,
  input  [7:0] B,
  input  [3:0] opcode,
  output [7:0] R
);

  wire adder_1_cout, not_1_out, or_1_out;
  wire [7:0] adder_1_out, and_1_out, bit_extender_1_out, bit_extender_2_out, multiplexer_1_out,
       negator_1_out, or_2_out, shifter_1_out, shifter_2_out;

  Negator negator_1 (.in(B), .out(negator_1_out));
  Multiplexer #(.width(8)) multiplexer_1 (.in0(negator_1_out), .in1(B), .out(multiplexer_1_out), .sel(opcode[0]));
  Adder adder_1 (.a(A), .b(multiplexer_1_out), .out(adder_1_out), .cin(1'b0), .cout(adder_1_cout));
  LED led_1 (.in(adder_1_cout));
  not not_1 (not_1_out, or_1_out);
  or or_1 (or_1_out, A[7], A[6], A[5], A[4], A[3], A[2], A[1], A[0]);
  assign and_1_out = A & B;  // AND_Gate and_1, 8 bits wide
  assign or_2_out = A | B;  // OR_Gate or_2, 8 bits wide
  assign bit_extender_1_out = {{7{1'b0}}, not_1_out};  // Bit_Extender bit_extender_1
  Shifter shifter_1 (.in(A), .\dist (B[2:0]), .out(shifter_1_out));
  Shifter #(.shift("lr")) shifter_2 (.in(A), .\dist (B[2:0]), .out(shifter_2_out));
  assign bit_extender_2_out = {{7{1'b0}}, or_1_out};  // Bit_Extender bit_extender_2
  Multiplexer #(.select(4), .width(8)) multiplexer_2 (
    .in0(bit_extender_2_out), .in1(bit_extender_2_out), .in2(B), .in3(B), .in4(B), .in5(B), .in6(B),
    .in7({B[3:0], A[3:0]}), .in8({A[7:4], B[3:0]}), .in9(adder_1_out), .in10(adder_1_out), .in11(and_1_out),
    .in12(or_2_out), .in13(bit_extender_1_out), .in14(shifter_1_out), .in15(shifter_2_out), .out(R),
    .sel(opcode));
endmodule

module PIPE_EXMD (
  input  [7:0] DA_in,
  input  Branch_in,
  input  [7:0] Res_in,
  input  Load_in,
  input  RWE_in,
  input  MWE_in,
  input  [7:0] PC_in,
  input  [1:0] RD_in,
  input  R,
  input  Clk,
  output [7:0] DA_out,
  output Branch_out,
  output [7:0] Res_out,
  output Load_out,
  output RWE_out,
  output MWE_out,
  output [7:0] PC_out,
  output [1:0] RD_out
);

  wire multiplexer_2_out, multiplexer_4_out, multiplexer_5_out, multiplexer_6_out;
  wire [1:0] multiplexer_8_out;
  wire [7:0] multiplexer_1_out, multiplexer_3_out, multiplexer_7_out;

  Register DA (.D(multiplexer_1_out), .en(1'b1), .clk(Clk), .Q(DA_out), .clr(1'b0));
  Multiplexer #(.width(8)) multiplexer_1 (.in0(DA_in), .in1({8{1'b0}}), .out(multiplexer_1_out), .sel(R));
  Register #(.width(1)) Branch (.D(multiplexer_2_out), .en(1'b1), .clk(Clk), .Q(Branch_out), .clr(1'b0));
  Multiplexer multiplexer_2 (.in0(Branch_in), .in1(1'b0), .out(multiplexer_2_out), .sel(R));
  Register Res (.D(multiplexer_3_out), .en(1'b1), .clk(Clk), .Q(Res_out), .clr(1'b0));
  Multiplexer #(.width(8)) multiplexer_3 (.in0(Res_in), .in1({8{1'b0}}), .out(multiplexer_3_out), .sel(R));
  Register #(.width(1)) Load (.D(multiplexer_4_out), .en(1'b1), .clk(Clk), .Q(Load_out), .clr(1'b0));
  Multiplexer multiplexer_4 (.in0(Load_in), .in1(1'b0), .out(multiplexer_4_out), .sel(R));
  Register #(.width(1)) RWE (.D(multiplexer_5_out), .en(1'b1), .clk(Clk), .Q(RWE_out), .clr(1'b0));
  Multiplexer multiplexer_5 (.in0(RWE_in), .in1(1'b0), .out(multiplexer_5_out), .sel(R));
  Register #(.width(1)) MWE (.D(multiplexer_6_out), .en(1'b1), .clk(Clk), .Q(MWE_out), .clr(1'b0));
  Multiplexer multiplexer_6 (.in0(MWE_in), .in1(1'b0), .out(multiplexer_6_out), .sel(R));
  Register PC (.D(multiplexer_7_out), .en(1'b1), .clk(Clk), .Q(PC_out), .clr(1'b0));
  Multiplexer #(.width(8)) multiplexer_7 (.in0(PC_in), .in1({8{1'b0}}), .out(multiplexer_7_out), .sel(R));
  Register #(.width(2)) RD (.D(multiplexer_8_out), .en(1'b1), .clk(Clk), .Q(RD_out), .clr(1'b0));
  Multiplexer #(.width(2)) multiplexer_8 (.in0(RD_in), .in1(2'b00), .out(multiplexer_8_out), .sel(R));
endmodule

module PIPE_MDWB (
  input  [7:0] Res_in,
  input  [7:0] Mem_in,
  input  Load_in,
  input  [1:0] RD_in,
  input  WE_in,
  input  Clk,
  input  R,
  output [7:0] Res_out,
  output [7:0] Mem_out,
  output Load_out,
  output [1:0] RD_out,
  output WE_out
);

  wire multiplexer_3_out, multiplexer_5_out;
  wire [1:0] multiplexer_4_out;
  wire [7:0] multiplexer_1_out, multiplexer_2_out;

  Register Res (.D(multiplexer_1_out), .en(1'b1), .clk(Clk), .Q(Res_out), .clr(R));
  Multiplexer #(.width(8)) multiplexer_1 (.in0(Res_in), .in1({8{1'b0}}), .out(multiplexer_1_out), .sel(R));
  Register Mem (.D(multiplexer_2_out), .en(1'b1), .clk(Clk), .Q(Mem_out), .clr(R));
  Multiplexer #(.width(8)) multiplexer_2 (.in0(Mem_in), .in1({8{1'b0}}), .out(multiplexer_2_out), .sel(R));
  Register #(.width(1)) Load (.D(multiplexer_3_out), .en(1'b1), .clk(Clk), .Q(Load_out), .clr(R));
  Multiplexer multiplexer_3 (.in0(Load_in), .in1(1'b0), .out(multiplexer_3_out), .sel(R));
  Register #(.width(2)) RD (.D(multiplexer_4_out), .en(1'b1), .clk(Clk), .Q(RD_out), .clr(R));
  Multiplexer #(.width(2)) multiplexer_4 (.in0(RD_in), .in1(2'b00), .out(multiplexer_4_out), .sel(R));
  Register #(.width(1)) WE (.D(multiplexer_5_out), .en(1'b1), .clk(Clk), .Q(WE_out), .clr(R));
  Multiplexer multiplexer_5 (.in0(WE_in), .in1(1'b0), .out(multiplexer_5_out), .sel(R));
endmodule

module c_register_bank (
  input  R,
  input  RC,
  input  [1:0] RA,
  input  [1:0] RB,
  input  FWE,
  input  [1:0] FRD,
  input  WE,
  input  [1:0] RD,
  input  [7:0] D,
  input  Clk,
  output Blk,
  output [7:0] DA,
  output [7:0] DB
);

  wire adder_1_cout, adder_2_cout, adder_3_cout, adder_4_cout, and_1_out, and_2_out, and_3_out, and_4_out,
       and_5_out, demultiplexer_1_out0, demultiplexer_1_out1, demultiplexer_1_out2, demultiplexer_1_out3,
       demultiplexer_2_out0, demultiplexer_2_out1, demultiplexer_2_out2, demultiplexer_2_out3,
       multiplexer_1_out, multiplexer_3_out, multiplexer_5_out, multiplexer_7_out, multiplexer_10_out,
       multiplexer_12_out, or_1_out, or_2_out, or_3_out, or_4_out, or_5_out, or_6_out, or_7_out, or_8_out,
       or_9_out;
  wire [1:0] adder_1_out, adder_2_out, adder_3_out, adder_4_out, multiplexer_2_out, multiplexer_4_out,
       multiplexer_6_out, multiplexer_8_out, R0C_q, R1C_q, R2C_q, R3C_q;
  wire [7:0] R0_q, R1_q, R2_q, R3_q;

  and and_1 (and_1_out, ~Blk, FWE);  // AND_Gate
  Demultiplexer #(.select(2)) demultiplexer_1 (
    .out0(demultiplexer_1_out0), .out1(demultiplexer_1_out1), .out2(demultiplexer_1_out2),
    .out3(demultiplexer_1_out3), .in(and_1_out), .sel(FRD));
  Demultiplexer #(.select(2)) demultiplexer_2 (
    .out0(demultiplexer_2_out0), .out1(demultiplexer_2_out1), .out2(demultiplexer_2_out2),
    .out3(demultiplexer_2_out3), .in(WE), .sel(RD));
  or or_1 (or_1_out, demultiplexer_1_out0, demultiplexer_2_out0);
  and and_2 (and_2_out, demultiplexer_2_out0, or_6_out);
  Multiplexer multiplexer_1 (.in0(1'b0), .in1(1'b1), .out(multiplexer_1_out), .sel(and_2_out));
  Adder #(.width(2)) adder_1 (
    .a(R0C_q), .b(multiplexer_2_out), .out(adder_1_out), .cin(multiplexer_1_out), .cout(adder_1_cout));
  Multiplexer #(.width(2)) multiplexer_2 (.in0(2'b01), .in1(2'b10), .out(multiplexer_2_out), .sel(and_2_out));
  LED led_1 (.in(adder_1_cout));
  or or_2 (or_2_out, demultiplexer_2_out1, demultiplexer_1_out1);
  and and_3 (and_3_out, demultiplexer_2_out1, or_7_out);
  Multiplexer multiplexer_3 (.in0(1'b0), .in1(1'b1), .out(multiplexer_3_out), .sel(and_3_out));
  Adder #(.width(2)) adder_2 (
    .a(R1C_q), .b(multiplexer_4_out), .out(adder_2_out), .cin(multiplexer_3_out), .cout(adder_2_cout));
  Multiplexer #(.width(2)) multiplexer_4 (.in0(2'b01), .in1(2'b10), .out(multiplexer_4_out), .sel(and_3_out));
  LED led_2 (.in(adder_2_cout));
  or or_3 (or_3_out, demultiplexer_2_out2, demultiplexer_1_out2);
  and and_4 (and_4_out, demultiplexer_2_out2, or_8_out);
  Multiplexer multiplexer_5 (.in0(1'b0), .in1(1'b1), .out(multiplexer_5_out), .sel(and_4_out));
  Adder #(.width(2)) adder_3 (
    .a(R2C_q), .b(multiplexer_6_out), .out(adder_3_out), .cin(multiplexer_5_out), .cout(adder_3_cout));
  Multiplexer #(.width(2)) multiplexer_6 (.in0(2'b01), .in1(2'b10), .out(multiplexer_6_out), .sel(and_4_out));
  LED led_3 (.in(adder_3_cout));
  or or_4 (or_4_out, demultiplexer_2_out3, demultiplexer_1_out3);
  and and_5 (and_5_out, demultiplexer_2_out3, or_9_out);
  Multiplexer multiplexer_7 (.in0(1'b0), .in1(1'b1), .out(multiplexer_7_out), .sel(and_5_out));
  Adder #(.width(2)) adder_4 (
    .a(R3C_q), .b(multiplexer_8_out), .out(adder_4_out), .cin(multiplexer_7_out), .cout(adder_4_cout));
  Multiplexer #(.width(2)) multiplexer_8 (.in0(2'b01), .in1(2'b10), .out(multiplexer_8_out), .sel(and_5_out));
  LED led_4 (.in(adder_4_cout));
  Register R0 (.D(D), .en(demultiplexer_2_out0), .clk(Clk), .Q(R0_q), .clr(R));
  Register #(.width(2)) R0C (.D(adder_1_out), .en(or_1_out), .clk(Clk), .Q(R0C_q), .clr(or_5_out));
  Register R1 (.D(D), .en(demultiplexer_2_out1), .clk(Clk), .Q(R1_q), .clr(R));
  Register #(.width(2)) R1C (.D(adder_2_out), .en(or_2_out), .clk(Clk), .Q(R1C_q), .clr(or_5_out));
  Register R2 (.D(D), .en(demultiplexer_2_out2), .clk(Clk), .Q(R2_q), .clr(R));
  Register #(.width(2)) R2C (.D(adder_3_out), .en(or_3_out), .clk(Clk), .Q(R2C_q), .clr(or_5_out));
  Register R3 (.D(D), .en(demultiplexer_2_out3), .clk(Clk), .Q(R3_q), .clr(R));
  Register #(.width(2)) R3C (.D(adder_4_out), .en(or_4_out), .clk(Clk), .Q(R3C_q), .clr(or_5_out));
  or or_5 (or_5_out, R, RC);
  Multiplexer #(.select(2), .width(8)) multiplexer_9 (
    .in0(R0_q), .in1(R1_q), .in2(R2_q), .in3(R3_q), .out(DA), .sel(RA));
  or or_6 (or_6_out, R0C_q[0], R0C_q[1]);
  or or_7 (or_7_out, R1C_q[0], R1C_q[1]);
  or or_8 (or_8_out, R2C_q[0], R2C_q[1]);
  or or_9 (or_9_out, R3C_q[0], R3C_q[1]);
  Multiplexer #(.select(2)) multiplexer_10 (
    .in0(or_6_out), .in1(or_7_out), .in2(or_8_out), .in3(or_9_out), .out(multiplexer_10_out), .sel(RA));
  Multiplexer #(.select(2), .width(8)) multiplexer_11 (
    .in0(R0_q), .in1(R1_q), .in2(R2_q), .in3(R3_q), .out(DB), .sel(RB));
  or or_10 (Blk, multiplexer_10_out, multiplexer_12_out);
  Multiplexer #(.select(2)) multiplexer_12 (
    .in0(or_6_out), .in1(or_7_out), .in2(or_8_out), .in3(or_9_out), .out(multiplexer_12_out), .sel(RB));
endmodule
